// Logisim project CPU Diagram.circ as structural Verilog: 1 circuit, main circuit main
module main (
);

  wire and_1_out, and_2_out, and_3_out, and_4_out, CLK, decoder_1_out0, decoder_1_out1, decoder_1_out2,
       decoder_1_out3, EQ1, EQ2, RESET, SEL_BP1, SEL_BP2, SUB_SEL;
  wire [1:0] RD_EX, RD_MEM, WB_RD;
  wire [3:0] OPCODE_EX;
  wire [7:0] A_EX, A_EX___B_EX, A_EX_OR_B_EX, A_EX_XOR_B_EX, adder_1_out, ALU_EX, ALU_MEM, B_ARITH, B_EX,
       DATA1_ID, DATA2_ID, NOT_A_OUT, NOT_B_OUT, PC_ID, PC_IF, R0_q, R1_q, R2_q, R3_q, RDAT1_RAW, RDAT2_RAW,
       SUM, WB_WD;
  wire [15:0] INSTR_ID, INSTR_IF;

  Button u_RESET (.out(RESET));
  Clock u_CLK (.out(CLK));
  Register IF_ID_PC (.D(PC_IF), .Q(PC_ID), .clk(CLK), .clr(RESET));  // open: en
  Register #(.width(4)) ID_EX_OPCODE (.D(INSTR_ID[15:12]), .Q(OPCODE_EX), .clk(CLK), .clr(RESET));  // open: en
  Register ID_EX_A (.D(DATA1_ID), .Q(A_EX), .clk(CLK), .clr(RESET));  // open: en
  Register ID_EX_B (.D(DATA2_ID), .Q(B_EX), .clk(CLK), .clr(RESET));  // open: en
  Register #(.width(2)) EX_MEM_RD (.D(RD_EX), .Q(RD_MEM), .clk(CLK), .clr(RESET));  // open: en
  Register #(.width(2)) MEM_WB_RD (.D(RD_MEM), .Q(WB_RD), .clk(CLK), .clr(RESET));  // open: en
  Register #(.width(16)) IF_ID_INSTR (.D(INSTR_IF), .Q(INSTR_ID), .clk(CLK), .clr(RESET));  // open: en
  Register PC (.D(adder_1_out), .Q(PC_IF), .clk(CLK), .clr(RESET));  // open: en
  Adder adder_1 (.a(8'h1), .b(PC_IF), .out(adder_1_out), .cin(1'b0));  // open: cout
  Register #(.width(2)) ID_EX_RD (.D(INSTR_ID[7:6]), .Q(RD_EX), .clk(CLK), .clr(RESET));  // open: en
  Register EX_MEM_ALU (.D(ALU_EX), .Q(ALU_MEM), .clk(CLK), .clr(RESET));  // open: en
  Register MEM_WB_DATA (.D(ALU_MEM), .Q(WB_WD), .clk(CLK), .clr(RESET));  // open: en
  ROM #(.dataWidth(16)) rom_1 (.addr(PC_IF), .data(INSTR_IF));  // open: sel
  Decoder #(.select(2)) decoder_1 (
    .out0(decoder_1_out0), .out1(decoder_1_out1), .out2(decoder_1_out2), .out3(decoder_1_out3), .sel(WB_RD));  // open: en
  and and_1 (and_1_out, decoder_1_out0, 1'b1);
  and and_2 (and_2_out, decoder_1_out1, 1'b1);
  and and_3 (and_3_out, decoder_1_out2, 1'b1);
  and and_4 (and_4_out, decoder_1_out3, 1'b1);
  Comparator #(.width(4)) comparator_1 (.a(OPCODE_EX), .b(4'b0001), .eq(SUB_SEL));  // open: gt, lt
  assign A_EX_XOR_B_EX = A_EX ^ B_EX;  // XOR_Gate xor_1, 8 bits wide
  assign A_EX_OR_B_EX = A_EX | B_EX;  // OR_Gate or_1, 8 bits wide
  assign A_EX___B_EX = A_EX & B_EX;  // AND_Gate and_5, 8 bits wide
  assign NOT_A_OUT = ~A_EX;  // NOT_Gate not_1, 8 bits wide
  assign NOT_B_OUT = ~B_EX;  // NOT_Gate not_2, 8 bits wide
  Multiplexer #(.width(8)) multiplexer_1 (.in0(B_EX), .in1(NOT_B_OUT), .out(B_ARITH), .sel(SUB_SEL));  // open: en
  Register R1 (.D(WB_WD), .en(and_2_out), .Q(R1_q), .clk(CLK), .clr(RESET));
  Register R0 (.D(WB_WD), .en(and_1_out), .Q(R0_q), .clk(CLK), .clr(RESET));
  Adder adder_2 (.a(A_EX), .b(B_ARITH), .out(SUM), .cin(SUB_SEL));  // open: cout
  Multiplexer #(.select(3), .width(8)) multiplexer_2 (
    .in0(SUM), .in1(SUM), .in2(NOT_A_OUT), .in3(A_EX___B_EX), .in4(A_EX_OR_B_EX), .in5(A_EX_XOR_B_EX),
    .in6({8{1'b0}}), .in7({8{1'b0}}), .out(ALU_EX), .sel(OPCODE_EX[2:0]));  // open: en
  Register R2 (.D(WB_WD), .en(and_3_out), .Q(R2_q), .clk(CLK), .clr(RESET));
  Register R3 (.D(WB_WD), .en(and_4_out), .Q(R3_q), .clk(CLK), .clr(RESET));
  Multiplexer #(.select(2), .width(8)) multiplexer_3 (
    .in0(R0_q), .in1(R1_q), .in2(R2_q), .in3(R3_q), .out(RDAT1_RAW), .sel(INSTR_ID[11:10]));  // open: en
  Multiplexer #(.select(2), .width(8)) multiplexer_4 (
    .in0(R0_q), .in1(R1_q), .in2(R2_q), .in3(R3_q), .out(RDAT2_RAW), .sel(INSTR_ID[9:8]));  // open: en
  Comparator #(.width(2)) comparator_2 (.a(WB_RD), .b(INSTR_ID[11:10]), .eq(EQ1));  // open: gt, lt
  Comparator #(.width(2)) comparator_3 (.a(WB_RD), .b(INSTR_ID[9:8]), .eq(EQ2));  // open: gt, lt
  and and_6 (SEL_BP1, EQ1, 1'b1);
  and and_7 (SEL_BP2, EQ2, 1'b1);
  Multiplexer #(.width(8)) multiplexer_5 (.in0(RDAT1_RAW), .in1(WB_WD), .out(DATA1_ID), .sel(SEL_BP1));  // open: en
  Multiplexer #(.width(8)) multiplexer_6 (.in0(RDAT2_RAW), .in1(WB_WD), .out(DATA2_ID), .sel(SEL_BP2));  // open: en

  // Other names for the same wires on the sheet: RD_ID[1:0] = INSTR_ID[7:6]; RS2_ID[1:0] = INSTR_ID[9:8];
  //   RS1_ID[1:0] = INSTR_ID[11:10]; OPCODE_ID[3:0] = INSTR_ID[15:12]; MEM_DATA[7:0] = ALU_MEM

  // Notes on the sheet:
  //   Constants
  //   STAGE:1 IF/ID Pipeline Registers
  //   STAGE 2: ID/EX Pipeline Register
  //   Stage 3: EX/MEM Pipeline Registers
  //   Stage 4,5: MEM/WB Pipeline Registers
  //   Program Counter and Incrementer
  //   Instruction ROM
  //   Instruction Split
  //   EXECUTE
  //   OPCODE SELECT
  //   INSTRUCTION DECODER
  //   READ MUX
endmodule
